// Logisim project lifebox-alert-logic.circ as structural Verilog: 1 circuit, main circuit main
// LifeBox 2050 - Logica Digital de Alerta
module main (
  input  TRANSPORTE_ATIVO,
  input  TEMPERATURA_CRITICA,
  input  IMPACTO_CRITICO,
  output ALERTA,
  output LED,
  output BUZZER
);

  wire CONDICAO_CRITICA_out;

  or CONDICAO_CRITICA (CONDICAO_CRITICA_out, TEMPERATURA_CRITICA, IMPACTO_CRITICO);
  and ALERTA_ATIVO (ALERTA, TRANSPORTE_ATIVO, CONDICAO_CRITICA_out);

  assign BUZZER = ALERTA;
  assign LED = ALERTA;
endmodule
